// Logisim project ControllerUnity.circ as structural Verilog: 4 circuits, main circuit ControllerUnity
module ControllerUnity (
  input  [5:0] OpCode,
  output [1:0] ALUOp,
  output RegDst,
  output WriteReg,
  output ALUSrc,
  output MemToReg,
  output MemRead,
  output MemWrite,
  output Branch,
  output Bne,
  output Jump,
  output Link
);

  wire Addi_out, Beq_out, J_out, or_1_out;
  wire [1:0] n1to00_1_s, n1to01_1_s, n1to01_2_s, n1to01_3_s, n1to10_1_s, n1to10_2_s, or_2_out;

  // Probe on OpCode
  Multiplexer #(.width(2), .enable("false")) multiplexer_1 (.in0(2'b11), .in1(or_2_out), .out(ALUOp), .sel(or_1_out));
  or or_1 (or_1_out, Bne, Beq_out, MemWrite, MemRead, Addi_out, RegDst);
  _1To00 u_1to00_1 (.A(RegDst), .S(n1to00_1_s));
  _1To01 u_1to01_1 (.A(Addi_out), .S(n1to01_1_s));
  _1To01 u_1to01_2 (.A(MemRead), .S(n1to01_2_s));
  assign or_2_out = n1to00_1_s | n1to01_1_s | n1to01_2_s | n1to01_3_s | n1to10_1_s | n1to10_2_s;  // OR_Gate or_2, 2 bits wide
  _1To01 u_1to01_3 (.A(MemWrite), .S(n1to01_3_s));
  _1To10 u_1to10_1 (.A(Beq_out), .S(n1to10_1_s));
  _1To10 u_1to10_2 (.A(Bne), .S(n1to10_2_s));
  and R (RegDst, ~OpCode[0], ~OpCode[1], ~OpCode[2], ~OpCode[3], ~OpCode[4], ~OpCode[5]);  // AND_Gate
  and Addi (Addi_out, ~OpCode[0], ~OpCode[1], ~OpCode[2], OpCode[3], ~OpCode[4], ~OpCode[5]);  // AND_Gate
  and LW (MemRead, OpCode[0], OpCode[1], ~OpCode[2], ~OpCode[3], ~OpCode[4], OpCode[5]);  // AND_Gate
  and SW (MemWrite, OpCode[0], OpCode[1], ~OpCode[2], OpCode[3], ~OpCode[4], OpCode[5]);  // AND_Gate
  and Beq (Beq_out, ~OpCode[0], ~OpCode[1], OpCode[2], ~OpCode[3], ~OpCode[4], ~OpCode[5]);  // AND_Gate
  and u_Bne (Bne, OpCode[0], ~OpCode[1], OpCode[2], ~OpCode[3], ~OpCode[4], ~OpCode[5]);  // AND_Gate
  and J (J_out, ~OpCode[0], OpCode[1], ~OpCode[2], ~OpCode[3], ~OpCode[4], ~OpCode[5]);  // AND_Gate
  and Jal (Link, OpCode[0], OpCode[1], ~OpCode[2], ~OpCode[3], ~OpCode[4], ~OpCode[5]);  // AND_Gate
  or or_3 (WriteReg, RegDst, Addi_out, MemRead, Link);
  or or_4 (ALUSrc, Addi_out, MemRead, MemWrite);
  or or_5 (Branch, Beq_out, Bne);
  or or_6 (Jump, J_out, Link);

  assign MemToReg = MemRead;
endmodule

module _1To00 (
  input  A,
  output [1:0] S
);

  wire [1:0] not_1_out;

  assign not_1_out = ~{2{A}};  // NOT_Gate not_1, 2 bits wide
  assign S = ~({2{A}} ^ not_1_out);  // XNOR_Gate xnor_1, 2 bits wide
endmodule

module _1To01 (
  input  A,
  output [1:0] S
);

  wire [1:1] not_1_out;

  not not_1 (not_1_out[1], A);
  Multiplexer #(.width(2), .enable("false")) multiplexer_1 (.in0({2{A}}), .in1({not_1_out[1], A}), .out(S), .sel(A));
endmodule

module _1To10 (
  input  A,
  output [1:0] S
);

  wire [0:0] not_1_out;

  not not_1 (not_1_out[0], A);
  Multiplexer #(.width(2), .enable("false")) multiplexer_1 (.in0({2{A}}), .in1({A, not_1_out[0]}), .out(S), .sel(A));
endmodule
