// Logisim project Datapath.circ as structural Verilog: 2 circuits, main circuit datapath
module datapath (
  output Overflow
);

  wire and_1_out, and_2_out, Bne, Branch, button_1_out, Clear, Clock, clock_1_out, JAL, JR, Jump, main_1_p3,
       MemRead, MemToReg, MemWrite, multiplexer_2_out, not_1_out, not_2_out, RegDst, ULASrc, WriteReg;
  wire [1:0] ULAop;
  wire [3:0] ulacontrollerunity_1_op;
  wire [4:0] decoder_1_rd, decoder_1_rs, decoder_1_rt, decoder_1_shamt, multiplexer_5_out, multiplexer_6_out;
  wire [5:0] decoder_1_funct, decoder_1_opcode;
  wire [15:0] decoder_1_imm;
  wire [25:0] decoder_1_addr;
  wire [29:0] extensor_1_out_2;
  wire [31:0] adder_1_out, adder_2_out, datamem_1_dados_lidos, main_1_p4, meminstr_1_instruction,
       multiplexer_1_out, multiplexer_3_out, multiplexer_4_out, multiplexer_7_out, multiplexer_8_out,
       multiplexer_9_out, n2conc_1_output, PC_q, registerfile_1_ld1, registerfile_1_ld2;
  wire [31:30] extensor_1_out_2_2;

  not not_1 (not_1_out, main_1_p3);
  Multiplexer #(.width(32), .enable("false")) multiplexer_1 (
    .in0(adder_2_out), .in1(adder_1_out), .out(multiplexer_1_out), .sel(and_1_out));
  Adder #(.width(32)) adder_1 (.a(adder_2_out), .b({extensor_1_out_2, 2'b00}), .out(adder_1_out));  // open: cin, cout
  and and_1 (and_1_out, multiplexer_2_out, Branch);
  Multiplexer #(.enable("false")) multiplexer_2 (.in0(main_1_p3), .in1(not_1_out), .out(multiplexer_2_out), .sel(Bne));
  Clock clock_1 (.out(clock_1_out));
  or or_1 (Clock, clock_1_out, button_1_out);
  Button button_1 (.out(button_1_out));
  Button button_2 (.out(Clear));
  Multiplexer #(.width(32), .enable("false")) multiplexer_3 (
    .in0(multiplexer_1_out), .in1(registerfile_1_ld1), .out(multiplexer_3_out), .sel(JR));
  _2conc u_2conc_1 (.ADDR(decoder_1_addr), .PC_4(adder_2_out), .OUTPUT(n2conc_1_output));
  Multiplexer #(.width(32), .enable("false")) multiplexer_4 (
    .in0(multiplexer_3_out), .in1(n2conc_1_output), .out(multiplexer_4_out), .sel(Jump));
  Register #(.width(32)) PC (.D(multiplexer_4_out), .en(1'b1), .Q(PC_q), .clk(Clock), .clr(Clear));
  Adder #(.width(32)) adder_2 (.a(32'h4), .b(PC_q), .out(adder_2_out));  // open: cin, cout
  MemInstr meminstr_1 (.PC_address(PC_q), .Instruction(meminstr_1_instruction));
  Decoder decoder_1 (
    .INST(meminstr_1_instruction), .FUNCT(decoder_1_funct), .SHAMT(decoder_1_shamt), .IMM(decoder_1_imm),
    .ADDR(decoder_1_addr), .RD(decoder_1_rd), .RT(decoder_1_rt), .RS(decoder_1_rs), .Opcode(decoder_1_opcode));
  ControllerUnity controllerunity_1 (
    .OpCode(decoder_1_opcode), .RegDst(RegDst), .WriteReg(WriteReg), .ALUSrc(ULASrc), .MemToReg(MemToReg),
    .MemRead(MemRead), .MemWrite(MemWrite), .Branch(Branch), .Bne(Bne), .Jump(Jump), .Link(JAL), .ALUOp(ULAop));
  Multiplexer #(.width(5), .enable("false")) multiplexer_5 (
    .in0(decoder_1_rt), .in1(decoder_1_rd), .out(multiplexer_5_out), .sel(RegDst));
  not not_2 (not_2_out, JR);
  RegisterFile registerfile_1 (
    .LR1(decoder_1_rs), .WD(multiplexer_7_out), .RegWrite(and_2_out), .LR2(decoder_1_rt),
    .WR(multiplexer_6_out), .LD1(registerfile_1_ld1), .LD2(registerfile_1_ld2), .Clock(Clock));
  Multiplexer #(.width(5), .enable("false")) multiplexer_6 (
    .in0(multiplexer_5_out), .in1({5{1'b1}}), .out(multiplexer_6_out), .sel(JAL));
  Multiplexer #(.width(32), .enable("false")) multiplexer_7 (
    .in0(multiplexer_9_out), .in1(adder_2_out), .out(multiplexer_7_out), .sel(JAL));
  Extensor extensor_1 (.in_1(decoder_1_imm), .out_2({extensor_1_out_2_2, extensor_1_out_2}));
  ULAControllerUnity ulacontrollerunity_1 (.Funct(decoder_1_funct), .Op(ulacontrollerunity_1_op), .ALUOp(ULAop));
  and and_2 (and_2_out, not_2_out, WriteReg);
  Multiplexer #(.width(32), .enable("false")) multiplexer_8 (
    .in0(registerfile_1_ld2), .in1({extensor_1_out_2_2, extensor_1_out_2}), .out(multiplexer_8_out),
    .sel(ULASrc));
  // ULA_main main_1: pin names not known; wires that end beside it: multiplexer_8_out, ulacontrollerunity_1_op, main_1_p3, main_1_p4, Overflow, decoder_1_shamt
  datamem datamem_1 (
    .\Endereço (main_1_p4), .Escreve_dado(registerfile_1_ld2), .Dados_lidos(datamem_1_dados_lidos),
    .MemWrite(MemWrite), .MemRead(MemRead), .clk(Clock));  // open: clear
  Multiplexer #(.width(32), .enable("false")) multiplexer_9 (
    .in0(main_1_p4), .in1(datamem_1_dados_lidos), .out(multiplexer_9_out), .sel(MemToReg));
  // Probe on multiplexer_9_out
endmodule

module _2conc (
  input  [25:0] ADDR,
  input  [31:0] PC_4,
  output [31:0] OUTPUT
);


  assign OUTPUT = {PC_4[31:28], {6{1'b0}}, ADDR[19:0], 2'b00};
endmodule
