// Logisim project Decoder.circ as structural Verilog: 1 circuit, main circuit Decoder
module Decoder (
  input  [31:0] in_1,
  output [25:0] ADDR,
  output [5:0] Opcode,
  output [5:0] FUNCT,
  output [4:0] SHAMT,
  output [4:0] RD,
  output [4:0] RT,
  output [4:0] RS,
  output [14:0] IMM
);


  assign ADDR = in_1[25:0];
  assign FUNCT = in_1[5:0];
  assign IMM = in_1[14:0];
  assign Opcode = in_1[31:26];
  assign RD = in_1[15:11];
  assign RS = in_1[25:21];
  assign RT = in_1[20:16];
  assign SHAMT = in_1[10:6];
endmodule
