// Logisim project MemoryData.circ as structural Verilog: 1 circuit, main circuit datamem
// Mem. dados
module datamem (
  input  [31:0] \Endereço ,
  input  [31:0] Escreve_dado,
  input  clk,
  input  clear,
  input  MemWrite,
  input  MemRead,
  output [31:0] Dados_lidos
);

  RAM #(.addrWidth(24), .dataWidth(32), .bus("separate"), .Select("high"), .simpleMode("false")) ram_1 (
    .addr(\Endereço [23:0]), .din(Escreve_dado), .data(Dados_lidos), .str(MemWrite), .clk(clk), .ld(MemRead),
    .clr(clear));  // open: sel
endmodule
