// Logisim project MemoryInst.circ as structural Verilog: 1 circuit, main circuit MemInstr
module MemInstr (
  input  [31:0] PC_address,
  output [31:0] Instruction
);

  ROM #(.addrWidth(24), .dataWidth(32)) rom_1 (.addr(PC_address[25:2]), .data(Instruction));  // open: sel

  // Notes on the sheet:
  //   contents of rom_1 (hex, n*v repeats v):
  //   8100026 929020 3e00008 23bdfff4 afbf0000 afb00004 afb10008 20120000 10a00003 c100001 20a5ffff
  //   8100008 121020 8fbf0000 8fb00004 8fb10008 23bd000c 3e00008 23bdffec afb00000 afb10004 afb20008
  //   afb3000c afb40010 7502a 20010001 142a0003 63040 20e7ffff 8100018 61820 8fb00000 8fb10004 8fb20008
  //   8fb3000c 8fb40010 23bd0014 3e00008 20100007 20110006 220402a 20010001 14280001 118822 200482a
  //   11200001 118022 102020 112820 c100003 29020 20130002 20140005 133020 143820 c100012 3a820 2409020
  //   2a0a820 8100039
endmodule
