// Logisim project SignalExtensor.circ as structural Verilog: 1 circuit, main circuit Extensor
module Extensor (
  input  [15:0] FUNCT,
  output [31:0] EXT
);


  assign EXT = {{17{FUNCT[15]}}, FUNCT[14:0]};
endmodule
