// Logisim project ULA.circ as structural Verilog: 5 circuits, main circuit main
module main (
  input  [31:0] A,
  input  [31:0] B,
  input  [4:0] SHAMT,
  input  [3:0] Op_ALU,
  output zero,
  output [31:0] S,
  output overflow
);

  wire comparator_1_lt;
  wire [31:0] adder_1_out, and_1_out, new_1_to_32_bits_1_saida, nor_1_out, or_1_out, shifter_1_out,
       shifter_2_out, subtractor_1_out, xor_1_out;

  Adder #(.width(32)) adder_1 (.a(A), .b(B), .out(adder_1_out));  // open: cin, cout
  Shifter #(.width(32)) shifter_1 (.in(B), .\dist (SHAMT), .out(shifter_1_out));
  Subtractor #(.width(32)) subtractor_1 (.a(A), .b(B), .out(subtractor_1_out));  // open: bin, bout
  Shifter #(.width(32), .shift("lr")) shifter_2 (.in(B), .\dist (SHAMT), .out(shifter_2_out));
  assign and_1_out = A & B;  // AND_Gate and_1, 32 bits wide
  assign or_1_out = A | B;  // OR_Gate or_1, 32 bits wide
  assign xor_1_out = A ^ B;  // XOR_Gate xor_1, 32 bits wide
  assign nor_1_out = ~(A | B);  // NOR_Gate nor_1, 32 bits wide
  Comparator #(.width(32)) comparator_1 (.a(A), .b(B), .lt(comparator_1_lt));  // open: gt, eq
  new_1_to_32_bits new_1_to_32_bits_1 (.Entrada(comparator_1_lt), .Saida(new_1_to_32_bits_1_saida));
  Multiplexer #(.select(4), .width(32), .enable("false")) multiplexer_1 (
    .in0(adder_1_out), .in1(shifter_1_out), .in2(subtractor_1_out), .in3(shifter_2_out), .in4(and_1_out),
    .in5(or_1_out), .in6(xor_1_out), .in7(nor_1_out), .in8({32{1'b0}}), .in9(new_1_to_32_bits_1_saida),
    .in10({32{1'b0}}), .in11({32{1'b0}}), .in12({32{1'b0}}), .in13({32{1'b0}}), .in14({32{1'b0}}),
    .in15({32{1'b0}}), .out(S), .sel(Op_ALU));
  overflow overflow_1 (.A(A), .B(B), .R(S), .Overflow(overflow), .Op(Op_ALU));
  _32b_equals_zero u_32b_equals_zero_1 (.R(S), .out_2(zero));
endmodule

module overflow (
  input  [31:0] A,
  input  [3:0] Op,
  input  [31:0] B,
  input  [31:0] R,
  output Overflow
);

  wire and_1_out, and_2_out, and_3_out, and_4_out, and_5_out, and_6_out, and_7_out, and_8_out, or_1_out,
       or_2_out;

  and and_1 (and_1_out, ~A[31], ~B[31], R[31]);  // AND_Gate
  and and_2 (and_2_out, A[31], B[31], ~R[31]);  // AND_Gate
  and and_3 (and_3_out, ~A[31], B[31], R[31]);  // AND_Gate
  or or_1 (or_1_out, and_3_out, and_4_out);
  and and_4 (and_4_out, A[31], ~B[31], ~R[31]);  // AND_Gate
  and and_5 (and_5_out, ~Op[3], ~Op[2], ~Op[1], ~Op[0]);  // AND_Gate
  and and_6 (and_6_out, and_5_out, or_2_out);
  or or_2 (or_2_out, and_1_out, and_2_out);
  and and_7 (and_7_out, or_1_out, and_8_out);
  and and_8 (and_8_out, ~Op[0], Op[1], ~Op[2], ~Op[3]);  // AND_Gate
  or or_3 (Overflow, and_6_out, and_7_out);
endmodule

module _32b_equals_zero (
  input  [31:0] R,
  output out_2
);

  and and_1 (out_2, ~R[31], ~R[30], ~R[29], ~R[28], ~R[27], ~R[26], ~R[25], ~R[24], ~R[23], ~R[22], ~R[21], ~R[20], ~R[19], ~R[18], ~R[17], ~R[16], ~R[15], ~R[14], ~R[13], ~R[12], ~R[11], ~R[10], ~R[9], ~R[8], ~R[7], ~R[6], ~R[5], ~R[4], ~R[3], ~R[2], ~R[1], ~R[0]);  // AND_Gate
endmodule

module _1_bit_to_32 (
  input  in_1,
  output [31:0] out_2
);


  assign out_2 = {32{in_1}};
endmodule

module new_1_to_32_bits (
  input  Entrada,
  output [31:0] Saida
);


  assign Saida = {{31{1'b0}}, Entrada};
endmodule
