// Logisim project ULAControllerUnity.circ as structural Verilog: 1 circuit, main circuit ULAControllerUnity
module ULAControllerUnity (
  input  [5:0] Funct,
  input  [1:0] ALUOp,
  output JR,
  output [3:0] Op
);

  wire add_out, addu_out, jalr_out, jr_out, or_2_out, or_6_out, slt_out, sltu_out, sub_out, subu_out;
  wire [0:0] sll_out;
  wire [1:1] or_3_out, srl_out;
  wire [2:2] and_out, nor_out, or_out, xor_out;
  wire [3:0] multiplexer_1_out, or_7_out;
  wire [3:3] or_4_out, or_5_out;

  // Probe on Funct
  and sll (sll_out[0], ~Funct[0], ~Funct[1], ~Funct[2], ~Funct[3], ~Funct[4], ~Funct[5]);  // AND_Gate
  and srl (srl_out[1], ~Funct[0], Funct[1], ~Funct[2], ~Funct[3], ~Funct[4], ~Funct[5]);  // AND_Gate
  and u_jr (jr_out, ~Funct[0], ~Funct[1], ~Funct[2], Funct[3], ~Funct[4], ~Funct[5]);  // AND_Gate
  and jalr (jalr_out, Funct[0], ~Funct[1], ~Funct[2], Funct[3], ~Funct[4], ~Funct[5]);  // AND_Gate
  and add (add_out, ~Funct[0], ~Funct[1], ~Funct[2], ~Funct[3], ~Funct[4], Funct[5]);  // AND_Gate
  and addu (addu_out, Funct[0], ~Funct[1], ~Funct[2], ~Funct[3], ~Funct[4], Funct[5]);  // AND_Gate
  and sub (sub_out, ~Funct[0], Funct[1], ~Funct[2], ~Funct[3], ~Funct[4], Funct[5]);  // AND_Gate
  and subu (subu_out, Funct[0], Funct[1], ~Funct[2], ~Funct[3], ~Funct[4], Funct[5]);  // AND_Gate
  and \and  (and_out[2], ~Funct[0], ~Funct[1], Funct[2], ~Funct[3], ~Funct[4], Funct[5]);  // AND_Gate
  and \or  (or_out[2], Funct[0], ~Funct[1], Funct[2], ~Funct[3], ~Funct[4], Funct[5]);  // AND_Gate
  and \xor  (xor_out[2], ~Funct[0], Funct[1], Funct[2], ~Funct[3], ~Funct[4], Funct[5]);  // AND_Gate
  and \nor  (nor_out[2], Funct[0], Funct[1], Funct[2], ~Funct[3], ~Funct[4], Funct[5]);  // AND_Gate
  and slt (slt_out, ~Funct[0], Funct[1], ~Funct[2], Funct[3], ~Funct[4], Funct[5]);  // AND_Gate
  and sltu (sltu_out, Funct[0], Funct[1], ~Funct[2], Funct[3], ~Funct[4], Funct[5]);  // AND_Gate
  or or_2 (or_2_out, add_out, addu_out);
  or or_3 (or_3_out[1], sub_out, subu_out);
  or or_4 (or_4_out[3], jr_out, jalr_out);
  or or_5 (or_5_out[3], slt_out, sltu_out);
  or or_6 (or_6_out, or_5_out[3], or_4_out[3], nor_out[2], xor_out[2], or_out[2], and_out[2], srl_out[1], or_3_out[1], sll_out[0], or_2_out);
  Multiplexer #(.width(4), .enable("false")) multiplexer_1 (
    .in0(4'b0000), .in1(or_7_out), .out(multiplexer_1_out), .sel(or_6_out));
  assign or_7_out = {or_5_out[3], 2'b00, or_5_out[3]} | {or_4_out[3], 3'b000} | {1'b0, {3{nor_out[2]}}} | {1'b0, {2{xor_out[2]}}, 1'b0} | {1'b0, or_out[2], 1'b0, or_out[2]} | {1'b0, and_out[2], 2'b00} | {2'b00, {2{srl_out[1]}}} | {2'b00, or_3_out[1], 1'b0} | {3'b000, sll_out[0]} | 4'b0000;  // OR_Gate or_7, 4 bits wide
  Multiplexer #(.select(2), .width(4), .enable("false")) multiplexer_2 (
    .in0(multiplexer_1_out), .in1(4'b0000), .in2(4'b0010), .in3(4'b1111), .out(Op), .sel(ALUOp));
  and and_2 (JR, ~Op[0], ~Op[1], ~Op[2], Op[3]);  // AND_Gate
endmodule
